// Logisim project aois4lab.circ as structural Verilog: 1 circuit, main circuit main
module main (
  input  in_1,
  input  in_2,
  input  in_3,
  input  in_4,
  input  in_5,
  input  in_6,
  input  in_7,
  input  in_8,
  input  in_9,
  output out_10,
  output out_11,
  output out_12,
  output out_13,
  output \Сумма ,
  output out_15,
  output out_16,
  output out_17
);

  wire and_1_out, and_2_out, and_3_out, and_4_out, and_5_out, and_6_out, and_7_out, and_8_out, and_9_out,
       and_10_out, and_11_out, and_12_out, and_13_out, and_14_out, and_15_out, and_16_out, and_17_out,
       and_18_out, and_19_out, and_20_out, not_1_out, not_2_out, not_3_out, not_4_out, or_1_out, or_4_out,
       or_7_out, or_10_out;

  and and_1 (and_1_out, in_5, in_6, in_1);
  or or_1 (or_1_out, in_5, in_6, in_1);
  and and_2 (and_2_out, in_1, in_5);
  and and_3 (and_3_out, in_6, in_5);
  and and_4 (and_4_out, in_1, in_6);
  and and_5 (and_5_out, or_1_out, not_1_out);
  or or_2 (out_10, and_2_out, and_3_out, and_4_out);
  or or_3 (out_16, and_1_out, and_5_out);
  not not_1 (not_1_out, out_10);
  and and_6 (and_6_out, in_4, in_9, out_10);
  or or_4 (or_4_out, in_4, in_9, out_10);
  and and_7 (and_7_out, out_10, in_4);
  and and_8 (and_8_out, in_9, in_4);
  and and_9 (and_9_out, out_10, in_9);
  and and_10 (and_10_out, or_4_out, not_2_out);
  or or_5 (out_11, and_7_out, and_8_out, and_9_out);
  or or_6 (out_15, and_6_out, and_10_out);
  not not_2 (not_2_out, out_11);
  and and_11 (and_11_out, in_3, in_8, out_11);
  or or_7 (or_7_out, in_3, in_8, out_11);
  and and_12 (and_12_out, out_11, in_3);
  and and_13 (and_13_out, in_8, in_3);
  and and_14 (and_14_out, out_11, in_8);
  and and_15 (and_15_out, or_7_out, not_3_out);
  or or_8 (out_12, and_12_out, and_13_out, and_14_out);
  or or_9 (\Сумма , and_11_out, and_15_out);
  not not_3 (not_3_out, out_12);
  and and_16 (and_16_out, in_7, in_2, out_12);
  or or_10 (or_10_out, in_7, in_2, out_12);
  and and_17 (and_17_out, out_12, in_7);
  and and_18 (and_18_out, in_2, in_7);
  and and_19 (and_19_out, out_12, in_2);
  and and_20 (and_20_out, or_10_out, not_4_out);
  or or_11 (out_17, and_17_out, and_18_out, and_19_out);
  or or_12 (out_13, and_16_out, and_20_out);
  not not_4 (not_4_out, out_17);

  // Notes on the sheet:
  //   1число
  //   2 число
endmodule
