// Logisim project aois4lab_bcd9.circ as structural Verilog: 1 circuit, main circuit main
module main (
  input  x1,
  input  x2,
  input  x3,
  input  x4,
  output Y1,
  output Y2,
  output Y3,
  output Y4
);

  wire and_1_out, and_2_out, and_3_out, and_4_out, and_5_out, not_1_out, not_2_out, not_3_out, not_4_out,
       or_1_out, or_2_out, or_3_out, or_4_out, or_5_out;

  not not_1 (not_1_out, x1);
  not not_2 (not_2_out, x2);
  not not_3 (not_3_out, x3);
  not not_4 (not_4_out, x4);
  and and_1 (and_1_out, not_1_out, x2, x3, x4);
  and and_2 (and_2_out, not_1_out, not_2_out, x3);
  or or_1 (or_1_out, not_1_out, x2, not_4_out);
  or or_2 (or_2_out, not_1_out, x2, not_3_out);
  or or_3 (or_3_out, not_1_out, not_2_out, x3, x4);
  and and_3 (and_3_out, not_1_out, x4, not_3_out);
  and and_4 (and_4_out, not_3_out, not_2_out, x4);
  and and_5 (and_5_out, not_1_out, x3, not_4_out);
  or or_4 (or_4_out, not_2_out, not_3_out, not_4_out);
  or or_5 (or_5_out, not_1_out, not_4_out);
  or or_6 (Y1, and_1_out, and_2_out);
  and and_6 (Y2, or_1_out, or_2_out, or_3_out);
  or or_7 (Y3, and_3_out, and_4_out, and_5_out);
  and and_7 (Y4, or_4_out, or_5_out);

  // Notes on the sheet:
  //   !x2
  //   !x3
  //   !x4
endmodule
