// Logisim project 5LR.circ as structural Verilog: 1 circuit, main circuit main
module main (
  input  V,
  output q1,
  output q2,
  output q3,
  output q4
);

  wire and_1_out, and_2_out, and_3_out, clock_1_out, not_1_out, not_2_out, not_3_out;

  and and_1 (and_1_out, V, not_3_out, not_2_out, not_1_out);
  and and_2 (and_2_out, V, not_3_out, not_2_out);
  and and_3 (and_3_out, V, not_3_out);
  not not_1 (not_1_out, q2);
  not not_2 (not_2_out, q3);
  not not_3 (not_3_out, q4);
  Clock clock_1 (.out(clock_1_out));
  T_Flip_Flop t_ff_1 (.clk(clock_1_out), .T(and_1_out), .Q(q1));  // open: Qn, preset, reset, en
  T_Flip_Flop t_ff_2 (.clk(clock_1_out), .T(and_2_out), .Q(q2));  // open: Qn, preset, reset, en
  T_Flip_Flop t_ff_3 (.clk(clock_1_out), .T(and_3_out), .Q(q3));  // open: Qn, preset, reset, en
  T_Flip_Flop t_ff_4 (.clk(clock_1_out), .T(V), .Q(q4));  // open: Qn, preset, reset, en

  // Notes on the sheet:
  //   h1
  //   h2
  //   h3
  //   h4
  //   q2*
  //   q3*
  //   q4*
endmodule
